// Logisim project ONE_COMPLEMENT_8BITS.circ as structural Verilog: 1 circuit, main circuit main
module main (
  input  [6:0] Magnitude,
  input  Sign,
  output [7:0] out_3
);

  xor bit_6 (out_3[6], Magnitude[6], Sign);
  xor bit_5 (out_3[5], Magnitude[5], Sign);
  xor bit_4 (out_3[4], Magnitude[4], Sign);
  xor bit_3 (out_3[3], Magnitude[3], Sign);
  xor bit_2 (out_3[2], Magnitude[2], Sign);
  xor bit_1 (out_3[1], Magnitude[1], Sign);
  xor bit_0 (out_3[0], Magnitude[0], Sign);

  assign out_3[7] = Sign;
endmodule
